// Logisim project CPU.circ as structural Verilog: 20 circuits, main circuit CPU
module CPU (
);

  wire add_c_out, and_1_out, and_2_out, and_3_out, and_4_out, and_5_out, and_6_out, and_7_out, button_1_out,
       clearMIcounter, clock, clock_1_out, clock_count_low_overflow, cmp_most_significant, cmp_not_null,
       cmp_null, cond_always, cond_neg, cond_not_null, cond_null, cond_pos, controlled_inverter_1_out,
       counterOverflow, edge_detect_1_s, enableAdd, enableAND, enableInc, enableNOT, enableOR, enableSHIFTL,
       enableSHIFTR, enableXOR, halt, incPC, invert_cond, loadA, loadALU, loadB, loadCmp, loadInstruction,
       loadMemAddr, loadPC, loadPC_after_cond, loadRAM, loadRet, loadU, not_1_out, not_2_out, not_3_out,
       not_4_out, not_5_out, not_6_out, not_8_out, not_9_out, or_1_out, or_2_out, or_5_out, or_7_out, outA,
       outALU, outB, outCmp, outMemAddr, outPC, outPCp1, outRAM, outRet, outSpecial_sw1, outU, por_1_out,
       reset, reset_out, storeRAM;
  wire [2:0] cmp_reg_o_2;
  wire [3:0] add_s, add_s_2, clock_count_high_value, clock_count_high_value_2, clock_count_low_value,
       clock_count_low_value_2, cmp_reg_o, ret_reg_o, ret_reg_o_2;
  wire [7:0] A, alu_reg_o, B, byteand_1_o, bytenot_1_o, byteor_1_y, bytexor_1_y, controlled_buffer_1_out,
       controlled_buffer_3_out, controlled_buffer_13_out, dipswitch_1_sw8, increment_1_o, instruction_reg_o,
       main_bus, mem_addr_bus, memory_dout, mi_counter_value, PC, pc_value_p1, shiftleft_1_o, shiftright_1_o,
       U, undriven, undriven_2;
  wire [31:6] rom_1_data;

  not not_1 (not_1_out, reset);
  assign controlled_buffer_1_out = storeRAM ? mem_addr_bus : 8'bz;  // Controlled_Buffer controlled_buffer_1
  assign controlled_buffer_1_out = loadRAM ? main_bus : 8'bz;  // Controlled_Buffer controlled_buffer_2
  assign controlled_buffer_3_out = storeRAM ? main_bus : 8'bz;  // Controlled_Buffer controlled_buffer_3
  and and_1 (and_1_out, clock, not_1_out);
  not not_2 (not_2_out, and_1_out);
  DipSwitch dipswitch_1 (
    .sw1(dipswitch_1_sw8[7]), .sw2(dipswitch_1_sw8[6]), .sw3(dipswitch_1_sw8[5]), .sw4(dipswitch_1_sw8[4]),
    .sw5(dipswitch_1_sw8[3]), .sw6(dipswitch_1_sw8[2]), .sw7(dipswitch_1_sw8[1]), .sw8(dipswitch_1_sw8[0]));
  Hex_Digit_Display hex_digit_display_1 (.value(controlled_buffer_1_out[7:4]));  // open: dp
  not not_3 (not_3_out, storeRAM);
  or or_1 (or_1_out, reset, clearMIcounter, 1'b0);
  DipSwitch #(.number(2)) outSpecial (.sw1(outSpecial_sw1));  // open: sw2
  Hex_Digit_Display hex_digit_display_2 (.value(controlled_buffer_1_out[3:0]));  // open: dp
  RAM #(.databus("bibus")) memory (
    .addr(controlled_buffer_1_out), .we(storeRAM), .oe(not_3_out), .clk(clock),
    .din(controlled_buffer_3_out), .dout(memory_dout));
  assign main_bus = outSpecial_sw1 ? dipswitch_1_sw8 : 8'bz;  // Controlled_Buffer controlled_buffer_4
  ByteRegisterSafer mem_addr_reg (.o(mem_addr_bus), .load(loadMemAddr), .clock(clock), .i(main_bus), .clear(reset));
  Hex_Digit_Display hex_digit_display_3 (.value(mem_addr_bus[7:4]));  // open: dp
  Hex_Digit_Display hex_digit_display_4 (.value(mem_addr_bus[3:0]));  // open: dp
  Counter8 mi_counter (
    .value(mi_counter_value), .inc(not_2_out), .clock(not_2_out), .clear(or_1_out));  // open: overflow, value_p1, in_5, load
  ByteRegisterSafer instruction_reg (
    .o(instruction_reg_o), .load(loadInstruction), .clock(clock), .i(main_bus), .clear(reset));
  Hex_Digit_Display hex_digit_display_5 (.value(memory_dout[7:4]));  // open: dp
  Hex_Digit_Display hex_digit_display_6 (.value(memory_dout[3:0]));  // open: dp
  Clock clock_1 (.out(clock_1_out));
  Button button_1 (.out(button_1_out));
  assign main_bus = outRAM ? memory_dout : 8'bz;  // Controlled_Buffer controlled_buffer_5
  assign main_bus = outMemAddr ? mem_addr_bus : 8'bz;  // Controlled_Buffer controlled_buffer_6
  Hex_Digit_Display hex_digit_display_7 (.value(instruction_reg_o[7:4]));  // open: dp
  Hex_Digit_Display hex_digit_display_8 (.value(instruction_reg_o[3:0]));  // open: dp
  POR #(.PorHighDuration(1)) por_1 (.out(por_1_out));
  or or_2 (or_2_out, clock_1_out, button_1_out);
  not not_4 (not_4_out, halt);
  Button u_reset (.out(reset_out));
  ROM #(.addrWidth(12), .dataWidth(32)) instruction_decoder (
    .addr({instruction_reg_o, mi_counter_value[3:0]}),
    .data({storeRAM, cond_pos, cond_not_null, enableInc, invert_cond, cond_null, cond_neg, cond_always, enableXOR, outPCp1, outCmp, loadCmp, loadALU, enableNOT, outB, outA, loadPC, outRet, loadRet, outMemAddr, loadMemAddr, loadInstruction, outALU, enableAdd, clearMIcounter, loadB, loadA, outRAM, outPC, loadRAM, incPC, halt}));
  edge_detect edge_detect_1 (.s(edge_detect_1_s), .i(por_1_out));
  and and_2 (and_2_out, or_2_out, not_4_out);
  Hex_Digit_Display hex_digit_display_9 (.value(main_bus[7:4]));  // open: dp
  Hex_Digit_Display hex_digit_display_10 (.value(main_bus[3:0]));  // open: dp
  ROM #(.addrWidth(12), .dataWidth(32)) rom_1 (
    .addr({instruction_reg_o, mi_counter_value[3:0]}),
    .data({rom_1_data, loadU, outU, enableAND, enableSHIFTR, enableSHIFTL, enableOR}));
  or or_3 (reset, edge_detect_1_s, reset_out);
  or or_4 (clock, reset, and_2_out);
  assign main_bus = reset ? {8{1'b0}} : 8'bz;  // Controlled_Buffer controlled_buffer_7
  LED led_1 (.in(clock));
  Hex_Digit_Display hex_digit_display_11 (.value(A[7:4]));  // open: dp
  Hex_Digit_Display hex_digit_display_12 (.value(A[3:0]));  // open: dp
  ByteRegisterSafer u_A (.o(A), .load(loadA), .clock(clock), .i(main_bus), .clear(reset));
  ByteRegisterSafer u_B (.o(B), .load(loadB), .clock(clock), .i(main_bus), .clear(reset));
  ByteRegisterSafer u_U (.o(U), .load(loadU), .clock(clock), .i(main_bus), .clear(reset));
  assign main_bus = outA ? A : 8'bz;  // Controlled_Buffer controlled_buffer_8
  Hex_Digit_Display hex_digit_display_13 (.value(B[7:4]));  // open: dp
  Hex_Digit_Display hex_digit_display_14 (.value(B[3:0]));  // open: dp
  Hex_Digit_Display hex_digit_display_15 (.value(U[7:4]));  // open: dp
  Hex_Digit_Display hex_digit_display_16 (.value(U[3:0]));  // open: dp
  Hex_Digit_Display hex_digit_display_17 (.value(PC[7:4]));  // open: dp
  Hex_Digit_Display hex_digit_display_18 (.value(PC[3:0]));  // open: dp
  Counter8 u_pc (
    .overflow(counterOverflow), .value(PC), .value_p1(pc_value_p1), .inc(incPC), .clock(clock),
    .in_5(main_bus), .clear(reset), .load(loadPC_after_cond));
  assign main_bus = outB ? B : 8'bz;  // Controlled_Buffer controlled_buffer_9
  assign main_bus = outU ? U : 8'bz;  // Controlled_Buffer controlled_buffer_10
  assign main_bus = outPCp1 ? pc_value_p1 : 8'bz;  // Controlled_Buffer controlled_buffer_11
  assign main_bus = outPC ? PC : 8'bz;  // Controlled_Buffer controlled_buffer_12
  Hex_Digit_Display hex_digit_display_19 (.value(add_s_2));  // open: dp
  Hex_Digit_Display hex_digit_display_20 (.value(add_s));  // open: dp
  RippleCarryAdder add (.c_out(add_c_out), .s({add_s_2, add_s}), .b(A), .a(B));
  LED led_2 (.in(add_c_out));
  ByteRegisterSafer ret_reg (.o({ret_reg_o_2, ret_reg_o}), .load(loadRet), .clock(clock), .i(main_bus), .clear(reset));
  and and_3 (and_3_out, cond_null, cmp_null);
  not not_5 (not_5_out, cmp_most_significant);
  and and_4 (and_4_out, cond_neg, cmp_most_significant);
  not not_6 (not_6_out, cond_not_null);
  and and_5 (and_5_out, cond_not_null, cmp_not_null);
  assign controlled_buffer_13_out = enableAdd ? {add_s_2, add_s} : 8'bz;  // Controlled_Buffer controlled_buffer_13
  Increment increment_1 (.o(increment_1_o), .i(main_bus));  // open: carry
  ByteOr byteor_1 (.a(main_bus), .b(B), .y(byteor_1_y));
  Hex_Digit_Display hex_digit_display_21 (.value(ret_reg_o_2));  // open: dp
  Hex_Digit_Display hex_digit_display_22 (.value(ret_reg_o));  // open: dp
  Hex_Digit_Display hex_digit_display_23 (.value({cmp_most_significant, cmp_reg_o_2}));  // open: dp
  ByteRegisterSafer cmp_reg (
    .o({cmp_most_significant, cmp_reg_o_2, cmp_reg_o}), .load(loadCmp), .clock(clock), .i(main_bus),
    .clear(reset));
  and and_6 (and_6_out, not_5_out, cond_pos);
  or or_5 (or_5_out, not_6_out, and_5_out);
  assign controlled_buffer_13_out = enableNOT ? bytenot_1_o : 8'bz;  // Controlled_Buffer controlled_buffer_14
  ByteNot bytenot_1 (.i(main_bus), .o(bytenot_1_o));
  assign controlled_buffer_13_out = enableXOR ? bytexor_1_y : 8'bz;  // Controlled_Buffer controlled_buffer_15
  ByteXor bytexor_1 (.a(main_bus), .b(B), .y(bytexor_1_y));
  assign controlled_buffer_13_out = enableInc ? increment_1_o : 8'bz;  // Controlled_Buffer controlled_buffer_16
  assign controlled_buffer_13_out = enableOR ? byteor_1_y : 8'bz;  // Controlled_Buffer controlled_buffer_17
  ShiftLeft shiftleft_1 (.i(main_bus), .o(shiftleft_1_o));  // open: carry
  assign controlled_buffer_13_out = enableSHIFTL ? shiftleft_1_o : 8'bz;  // Controlled_Buffer controlled_buffer_18
  ShiftRight shiftright_1 (.i(main_bus), .o(shiftright_1_o));  // open: carry
  assign controlled_buffer_13_out = enableSHIFTR ? shiftright_1_o : 8'bz;  // Controlled_Buffer controlled_buffer_19
  assign controlled_buffer_13_out = enableAND ? byteand_1_o : 8'bz;  // Controlled_Buffer controlled_buffer_20
  ByteAnd byteand_1 (.a(main_bus), .b(B), .o(byteand_1_o));
  assign main_bus = outRet ? {ret_reg_o_2, ret_reg_o} : 8'bz;  // Controlled_Buffer controlled_buffer_21
  Hex_Digit_Display hex_digit_display_24 (.value(cmp_reg_o));  // open: dp
  or or_6 (cmp_not_null, cmp_most_significant, cmp_reg_o_2[2], cmp_reg_o_2[1], cmp_reg_o_2[0], cmp_reg_o[3], cmp_reg_o[2], cmp_reg_o[1], cmp_reg_o[0]);
  not not_7 (cmp_null, cmp_not_null);
  and and_7 (and_7_out, and_4_out, or_5_out);
  assign main_bus = outCmp ? {cmp_most_significant, cmp_reg_o_2, cmp_reg_o} : 8'bz;  // Controlled_Buffer controlled_buffer_22
  or or_7 (or_7_out, cond_always, and_3_out, and_6_out, and_7_out);
  Hex_Digit_Display hex_digit_display_25 (.value(controlled_buffer_13_out[7:4]));  // open: dp
  Hex_Digit_Display hex_digit_display_26 (.value(controlled_buffer_13_out[3:0]));  // open: dp
  assign controlled_inverter_1_out = invert_cond ? ~or_7_out : 1'bz;  // Controlled_Inverter controlled_inverter_1
  assign controlled_inverter_1_out = not_8_out ? or_7_out : 1'bz;  // Controlled_Buffer controlled_buffer_23
  not not_8 (not_8_out, invert_cond);
  Hex_Digit_Display hex_digit_display_27 (.value(alu_reg_o[7:4]));  // open: dp
  Hex_Digit_Display hex_digit_display_28 (.value(alu_reg_o[3:0]));  // open: dp
  ByteRegisterSafer alu_reg (.o(alu_reg_o), .load(loadALU), .clock(clock), .i(controlled_buffer_13_out), .clear(reset));
  and and_8 (loadPC_after_cond, loadPC, controlled_inverter_1_out);
  assign main_bus = outALU ? alu_reg_o : 8'bz;  // Controlled_Buffer controlled_buffer_24
  not not_9 (not_9_out, clock);
  // NoConnect on undriven
  Counter8 clock_count_low (
    .overflow(clock_count_low_overflow), .value({clock_count_low_value_2, clock_count_low_value}),
    .inc(not_9_out), .clock(clock), .in_5(undriven), .clear(reset), .load(1'b0));  // open: value_p1
  // NoConnect on undriven_2
  Hex_Digit_Display hex_digit_display_29 (.value(clock_count_high_value_2));  // open: dp
  Counter8 clock_count_high (
    .value({clock_count_high_value_2, clock_count_high_value}), .inc(clock_count_low_overflow),
    .clock(clock), .in_5(undriven_2), .clear(reset), .load(1'b0));  // open: overflow, value_p1
  Hex_Digit_Display hex_digit_display_30 (.value(clock_count_high_value));  // open: dp
  Hex_Digit_Display hex_digit_display_31 (.value(clock_count_low_value_2));  // open: dp
  Hex_Digit_Display hex_digit_display_32 (.value(clock_count_low_value));  // open: dp

  // Other names for the same wires on the sheet: strong_bit = main_bus[7]

  // Notes on the sheet:
  //   contents of instruction_decoder (hex, n*v repeats v):
  //   c 412 80 13*0 c 412 c 32 80 11*0 c 412 1 13*0 c 412 c 32 c 52 80100 220 80 7*0 c 412 c 810 1004 32 c
  //   810 1004 52 80100 220 80 0 0 0 c 412 c 50 80100 222 80 9*0 c 412 c 1008010 80 11*0 c 412 d0000
  //   10080200 220 80 10*0 c 412 c 52 80 11*0 c 412 20020 80 12*0 c 412 10040 80 12*0 c 412 e0000 10080200
  //   240 80 10*0 c 412 c 812 1004 50 e0000 10080200 240 80100 220 80 4*0 c 412 c 812 1004 50 e0000
  //   10080200 240 80100 100200 80 4*0 c 412 c 2 22008010 80 10*0 c 412 c 2 60008010 80 10*0 c 412 c 2
  //   4008010 80 10*0 c 412 c 2 c008010 80 10*0 c 412 c 2 6008010 80 10*0 c 412 c 2 44008010 80 10*0 c 412
  //   c 812 1004 30 80 9*0 c 412 c 812 1004 50 80 9*0 c 412 c 812 80020000 80 10*0 c 412 c 812 80010000 80
  //   10*0 c 412 c 812 80400000 80 10*0 c 412 10090000 220 80 11*0 c 412 c 812 2008 1009000 80 9*0 c 412
  //   100c000 80 12*0 c 412 c 812 1004 50 80100 220 80 7*0 c 412 890000 220 80 11*0 c 412 10040 890000 220
  //   80 10*0 c 412 c 812 1004 50 c 812 80020000 80 6*0 c 412 90000 220 80 11*0 c 412 90000 220 80 11*0 c
  //   412 90000 220 80 11*0 c 412 a0000 240 80 11*0 c 412 90000 220 80 11*0 c 412 a0000 240 80 11*0 c 412
  //   c 812 c 80000012 80 9*0 c 412 100a0000 240 80 11*0 c 412 c 812 1004 10080010 80000200 80 8*0 c 412
  //   80 13*0 c 412 c 810 1004 1008010 80 9*0 c 412 e0000 10080200 240 80100 100200 80 8*0 c 412 c 52
  //   e0000 10080200 240 80100 100200 80 6*0 c 412 10080000 200 80 11*0 c 412 c 812 1004 10 80 9*0 c 412 c
  //   812 80000000 80 10*0 c 412 40 880000 200 80 10*0 c 412 80000 200 80 11*0 c 412 80000 200 80 11*0 c
  //   412 d0000 220 80 11*0 c 412 e0000 240 80 11*0 c 412 c0000 200 80 11*0 c 412 c0000 10080200 200 80
  //   10*0 c 412 c 810 1006 c0010 10080200 80000200 80 7*0 c 412 10000 80 12*0 c 412 20000 80 12*0 c 412
  //   20 80 12*0 c 412 40 80 12*0 c 412 c 10 80 11*0 c 412 c 812 1004 50 80100 200 80 7*0 c 412 80 13*0 c
  //   412 80 13*0 c 412 80 13*0 c 412 80 13*0 c 412 80 13*0 c 412 80 13*0 c 412 80 13*0 c 412 80 13*0 c
  //   412 80 13*0 c 412 80 13*0 c 412 80 13*0 c 412 80 13*0 c 412 80 13*0 c 412 80 13*0 c 412 80 13*0 c
  //   412 80 13*0 c 412 80 13*0 c 412 80 13*0 c 412 80 13*0 c 412 80 13*0 c 412 80 13*0 c 412 80 13*0 c
  //   412 80 13*0 c 412 80 13*0 c 412 80 13*0 c 412 80 13*0 c 412 80 13*0 c 412 80 13*0 c 412 80 13*0 c
  //   412 80 13*0 c 412 80 13*0 c 412 80 13*0 c 412 80 13*0 c 412 80 13*0 c 412 80 13*0 c 412 80 13*0 c
  //   412 80 13*0 c 412 80 13*0 c 412 80 13*0 c 412 80 13*0 c 412 80 13*0 c 412 80 13*0 c 412 80 13*0 c
  //   412 80 13*0 c 412 80 13*0 c 412 80 13*0 c 412 80 13*0 c 412 80 13*0 c 412 80 13*0 c 412 80 13*0 c
  //   412 80 13*0 c 412 80 13*0 c 412 80 13*0 c 412 80 13*0 c 412 80 13*0 c 412 80 13*0 c 412 80 13*0 c
  //   412 80 13*0 c 412 80 13*0 c 412 80 13*0 c 412 80 13*0 c 412 80 13*0 c 412 80 13*0 c 412 80 13*0 c
  //   412 80 13*0 c 412 80 13*0 c 412 80 13*0 c 412 80 13*0 c 412 80 13*0 c 412 80 13*0 c 412 80 13*0 c
  //   412 80 13*0 c 412 80 13*0 c 412 80 13*0 c 412 80 13*0 c 412 80 13*0 c 412 80 13*0 c 412 80 13*0 c
  //   412 80 13*0 c 412 80 13*0 c 412 80 13*0 c 412 80 13*0 c 412 80 13*0 c 412 80 13*0 c 412 80 13*0 c
  //   412 80 13*0 c 412 80 13*0 c 412 80 13*0 c 412 80 13*0 c 412 80 13*0 c 412 80 13*0 c 412 80 13*0 c
  //   412 80 13*0 c 412 80 13*0 c 412 80 13*0 c 412 80 13*0 c 412 80 13*0 c 412 80 13*0 c 412 80 13*0 c
  //   412 80 13*0 c 412 80 13*0 c 412 80 13*0 c 412 80 13*0 c 412 80 13*0 c 412 80 13*0 c 412 80 13*0 c
  //   412 80 13*0 c 412 80 13*0 c 412 80 13*0 c 412 80 13*0 c 412 80 13*0 c 412 80 13*0 c 412 80 13*0 c
  //   412 80 13*0 c 412 80 13*0 c 412 80 13*0 c 412 80 13*0 c 412 80 13*0 c 412 80 13*0 c 412 80 13*0 c
  //   412 80 13*0 c 412 80 13*0 c 412 80 13*0 c 412 80 13*0 c 412 80 13*0 c 412 80 13*0 c 412 80 13*0 c
  //   412 80 13*0 c 412 80 13*0 c 412 80 13*0 c 412 80 13*0 c 412 80 13*0 c 412 80 13*0 c 412 80 13*0 c
  //   412 80 13*0 c 412 80 13*0 c 412 80 13*0 c 412 80 13*0 c 412 80 13*0 c 412 80 13*0 c 412 80 13*0 c
  //   412 80 13*0 c 412 80 13*0 c 412 80 13*0 c 412 80 13*0 c 412 80 13*0 c 412 80 13*0 c 412 80 13*0 c
  //   412 80 13*0 c 412 80 13*0 c 412 80 13*0 c 412 80 13*0 c 412 80 13*0 c 412 80 13*0 c 412 80 13*0 c
  //   412 80 13*0 c 412 80 13*0 c 412 80 13*0 c 412 80 13*0 c 412 80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
  //   contents of rom_1 (hex, n*v repeats v):
  //   514*0 1 15*0 8 15*0 2 15*0 2 15*0 4 15*0 4 127*0 10 20 17*0 20 14*0 10 13*0 10 10 20 13*0 11 20 14*0
  //   18 20 46*0 10 20 14*0 10 0 20 29*0 20 15*0 20 15*0 10 15*0 10 16*0 20 19*0 20
endmodule

module Half_Add (
  input  a,
  input  b,
  output y,
  output c
);

  xor xor_1 (y, a, b);
  and and_1 (c, b, a);
endmodule

module Full_Add (
  input  a,
  input  b,
  input  c_in,
  output y,
  output c_out
);

  wire and_1_out, and_2_out, xor_1_out;

  xor xor_1 (xor_1_out, a, b);
  and and_1 (and_1_out, a, b);
  xor xor_2 (y, xor_1_out, c_in);
  and and_2 (and_2_out, xor_1_out, c_in);
  or or_1 (c_out, and_2_out, and_1_out);
endmodule

// add
module RippleCarryAdder (
  input  [7:0] a,
  input  [7:0] b,
  output [7:0] s,
  output c_out
);

  wire full_add_1_c_out, full_add_2_c_out, full_add_3_c_out, full_add_4_c_out, full_add_5_c_out,
       full_add_6_c_out, full_add_7_c_out;

  Full_Add full_add_1 (.y(s[0]), .c_out(full_add_1_c_out), .a(a[0]), .b(b[0]), .c_in(1'b0));
  Full_Add full_add_2 (.y(s[1]), .c_out(full_add_2_c_out), .a(a[1]), .b(b[1]), .c_in(full_add_1_c_out));
  Full_Add full_add_3 (.y(s[2]), .c_out(full_add_3_c_out), .a(a[2]), .b(b[2]), .c_in(full_add_2_c_out));
  Full_Add full_add_4 (.y(s[3]), .c_out(full_add_4_c_out), .a(a[3]), .b(b[3]), .c_in(full_add_3_c_out));
  Full_Add full_add_5 (.y(s[4]), .c_out(full_add_5_c_out), .a(a[4]), .b(b[4]), .c_in(full_add_4_c_out));
  Full_Add full_add_6 (.y(s[5]), .c_out(full_add_6_c_out), .a(a[5]), .b(b[5]), .c_in(full_add_5_c_out));
  Full_Add full_add_7 (.y(s[6]), .c_out(full_add_7_c_out), .a(a[6]), .b(b[6]), .c_in(full_add_6_c_out));
  Full_Add full_add_8 (.y(s[7]), .c_out(c_out), .a(a[7]), .b(b[7]), .c_in(full_add_7_c_out));
endmodule

module SR_latch (
  input  s,
  input  r,
  output q,
  output not_q
);

  nor nor_1 (q, s, not_q);
  nor nor_2 (not_q, q, r);
endmodule

module D_latch (
  input  d,
  input  enable,
  output q
);

  wire and_1_out, and_2_out, nor_2_out, not_1_out;

  not not_1 (not_1_out, d);
  and and_1 (and_1_out, not_1_out, enable);
  and and_2 (and_2_out, enable, d);
  nor nor_1 (q, and_1_out, nor_2_out);
  nor nor_2 (nor_2_out, q, and_2_out);
endmodule

module AND_gate (
  input  a,
  input  b,
  output y
);

  wire transistor_1_out;

  Transistor #(.\type ("n")) transistor_1 (.in(1'b1), .out(transistor_1_out), .gate(a));
  Transistor #(.\type ("n")) transistor_2 (.in(transistor_1_out), .out(y), .gate(b));
  Pull_Resistor pull_resistor_1 (.node(y));
endmodule

module edge_detect (
  input  i,
  output s
);

  wire not_1_out, not_2_out, not_3_out;

  not not_1 (not_1_out, i);
  not not_2 (not_2_out, not_1_out);
  not not_3 (not_3_out, not_2_out);
  and and_1 (s, i, not_3_out);
endmodule

module D_flipflop (
  input  d,
  input  clock,
  output q
);

  wire edge_detect_1_s;

  edge_detect edge_detect_1 (.s(edge_detect_1_s), .i(clock));
  D_latch d_latch_1 (.d(d), .enable(edge_detect_1_s), .q(q));
endmodule

module ByteRegister (
  input  clock,
  input  load,
  input  enable,
  input  [7:0] i,
  output [7:0] s
);

  wire and_1_out;
  wire [7:0] undriven;

  and and_1 (and_1_out, clock, load);
  // D_flipflop d_flipflop_1: pin names not known; wires that end beside it: i[0], and_1_out
  // D_flipflop d_flipflop_2: pin names not known; wires that end beside it: i[1], and_1_out
  // D_flipflop d_flipflop_3: pin names not known; wires that end beside it: i[2], and_1_out
  // D_flipflop d_flipflop_4: pin names not known; wires that end beside it: i[3], and_1_out
  // D_flipflop d_flipflop_5: pin names not known; wires that end beside it: i[4], and_1_out
  // D_flipflop d_flipflop_6: pin names not known; wires that end beside it: i[5], and_1_out
  // D_flipflop d_flipflop_7: pin names not known; wires that end beside it: i[6], and_1_out
  // D_flipflop d_flipflop_8: pin names not known; wires that end beside it: i[7], and_1_out
  assign s = enable ? undriven : 8'bz;  // Controlled_Buffer controlled_buffer_1
endmodule

module Increment (
  input  [7:0] i,
  output carry,
  output [7:0] o
);

  wire half_add_2_c, half_add_3_c, half_add_4_c, half_add_5_c, half_add_6_c, half_add_7_c, half_add_8_c;

  Half_Add half_add_1 (.a(half_add_2_c), .b(i[7]), .y(o[7]), .c(carry));
  Half_Add half_add_2 (.a(half_add_3_c), .b(i[6]), .y(o[6]), .c(half_add_2_c));
  Half_Add half_add_3 (.a(half_add_4_c), .b(i[5]), .y(o[5]), .c(half_add_3_c));
  Half_Add half_add_4 (.a(half_add_5_c), .b(i[4]), .y(o[4]), .c(half_add_4_c));
  Half_Add half_add_5 (.a(half_add_6_c), .b(i[3]), .y(o[3]), .c(half_add_5_c));
  Half_Add half_add_6 (.a(half_add_7_c), .b(i[2]), .y(o[2]), .c(half_add_6_c));
  Half_Add half_add_7 (.a(half_add_8_c), .b(i[1]), .y(o[1]), .c(half_add_7_c));
  Half_Add half_add_8 (.a(1'b1), .b(i[0]), .y(o[0]), .c(half_add_8_c));
endmodule

module ByteRegisterSafe (
  input  clock,
  input  load,
  input  clear,
  input  [7:0] i,
  output [7:0] o
);

  wire and_1_out, n74273_1_pin1;

  and and_1 (and_1_out, clock, load);
  _74273 u_74273_1 (
    .pin1(n74273_1_pin1), .pin2(o[0]), .pin3(i[0]), .pin4(i[1]), .pin5(o[1]), .pin6(o[2]), .pin7(i[2]),
    .pin8(i[3]), .pin9(o[3]), .pin19(o[7]), .pin18(i[7]), .pin17(i[6]), .pin16(o[6]), .pin15(o[5]),
    .pin14(i[5]), .pin13(i[4]), .pin12(o[4]), .pin11(and_1_out));
  not not_1 (n74273_1_pin1, clear);
endmodule

module Counter8 (
  input  clock,
  input  load,
  input  inc,
  input  clear,
  input  [7:0] in_5,
  output [7:0] value,
  output overflow,
  output [7:0] value_p1
);

  wire or_1_out;
  wire [7:0] controlled_buffer_1_out;

  or or_1 (or_1_out, load, inc);
  assign controlled_buffer_1_out = load ? in_5 : 8'bz;  // Controlled_Buffer controlled_buffer_1
  assign controlled_buffer_1_out = inc ? value_p1 : 8'bz;  // Controlled_Buffer controlled_buffer_2
  ByteRegisterSafe byteregistersafe_1 (
    .clock(clock), .load(or_1_out), .clear(clear), .i(controlled_buffer_1_out), .o(value));
  Increment increment_1 (.carry(overflow), .o(value_p1), .i(value));
endmodule

module ByteNot (
  input  [7:0] i,
  output [7:0] o
);

  assign o = ~i;  // NOT_Gate not_1, 8 bits wide
endmodule

module ByteXor (
  input  [7:0] a,
  input  [7:0] b,
  output [7:0] y
);

  assign y = a ^ b;  // XOR_Gate xor_1, 8 bits wide
endmodule

module ByteOr (
  input  [7:0] a,
  input  [7:0] b,
  output [7:0] y
);

  assign y = a | b;  // OR_Gate or_1, 8 bits wide
endmodule

module ShiftLeft (
  input  [7:0] i,
  output carry,
  output [7:0] o
);


  assign carry = i[7];
  assign o = {i[6:0], 1'b0};
endmodule

module ShiftRight (
  input  [7:0] i,
  output carry,
  output [7:0] o
);


  assign carry = i[0];
  assign o = {1'b0, i[7:1]};
endmodule

module ByteAnd (
  input  [7:0] a,
  input  [7:0] b,
  output [7:0] o
);

  assign o = a & b;  // AND_Gate and_1, 8 bits wide
endmodule

module ByteRegisterSafer (
  input  [7:0] i,
  input  load,
  input  clock,
  input  clear,
  output [7:0] o
);

  Register register_1 (.D(i), .en(load), .clk(clock), .Q(o), .clr(clear));
endmodule
